# Fritzing sketch MCU_module (saved by Fritzing 0.9.4)
breadboards: 1

parts:
  Part1 = Arduino Pro Mini v13
  J1 = screw terminal, 3 pins
  J2 = Screw terminal - 2 pins [package=THT]
  Q2 = MOSFET-NCHANNEL [package=to220v]
  J3 = screw terminal, 3 pins

nets:
  5V: Part1.VCC, J1.pin1, J3.pin1
  GND: Part1.GND, J1.pin3, Q2.S, J3.pin3
  N1: Part1.A2, Q2.G
  N2: Part1.A0, J1.pin2
  N3: Part1.D2, J3.pin2
  12V: J2.pin1
