# Fritzing sketch all in one schem (saved by Fritzing 0.9.4)
breadboards: 1

parts:
  Part2 = Arduino Pro Mini v13
  Q3 = MOSFET-NCHANNEL [package=to220v]
  J4 = screw terminal, 3 pins
  J5 = Screw terminal - 2 pins [package=THT]
  J6 = screw terminal, 3 pins
  PIR5 = PIR sensor
  PIR6 = PIR sensor
  PIR7 = PIR sensor
  R2 = Resistor [tolerance=±5% resistance=1k package=THT]
  D4 = Diode [package=diode-1n4148]
  D5 = Diode [package=diode-1n4148]
  D6 = Diode [package=diode-1n4148]
  J7 = screw terminal, 3 pins
  Q4 = NPN-Transistor [package="TO92 [THT]"]
  R6 = Resistor [tolerance=±5% resistance=1k package=THT]
  U3 = 555 Timer [package="DIP8 [THT]"]
  C5 = Ceramic Capacitor [capacitance=0.1nF package="100 mil [THT, multilayer]"]  # not connected
  C6 = Ceramic Capacitor [capacitance=1nF package="100 mil [THT, multilayer]"]
  C7 = Electrolytic Capacitor [capacitance=1µF package="100 mil [THT, electrolytic]"]
  R7 = Resistor [tolerance=±5% resistance=220 package=THT]
  R8 = Resistor [tolerance=±5% resistance=220 package=THT]
  Piezo3 = Piezo Speaker
  Piezo4 = Piezo Speaker
  J8 = screw terminal, 3 pins
  LED6 = LED - 5mm [color="Red (633nm)" package="5 mm [THT]"]
  LED7 = LED - 5mm [color="Red (633nm)" package="5 mm [THT]"]
  LED8 = LED - 5mm [color="Red (633nm)" package="5 mm [THT]"]
  LED9 = LED - 5mm [color="Red (633nm)" package="5 mm [THT]"]
  LED10 = LED - 5mm [color="Red (633nm)" package="5 mm [THT]"]
  R9 = Resistor [tolerance=±5% resistance=220 package=THT]
  J9 = Screw terminal - 2 pins [package=THT]

nets:
  5V: Part2.VCC, J4.pin1, J6.pin1, PIR5.VDD, PIR6.VDD, PIR7.VDD, J7.pin1
  GND: Part2.GND, Q3.S, J4.pin3, J6.pin3, PIR5.GND, PIR6.GND, PIR7.GND, R2.Pin_0, J7.pin3, Q4.E, C6.0, C7.-, Piezo3.pin2, Piezo4.pin2, J8.pin3
  N1: Part2.A2, Q3.G
  N2: Part2.A0, J4.pin2
  N3: Part2.D2, J6.pin2
  12V: J5.pin1, U3.Vcc_Supply_Voltage
  N4: PIR5.SIG, D6.A
  N5: PIR6.SIG, D5.A
  N6: PIR7.SIG, D4.A
  N7: R2.Pin_1, D4.C, D5.C, D6.C, J7.pin2
  N8: Q4.B, R6.Pin_1
  N9: Q4.C, U3.Ground
  N10: R6.Pin_0, J8.pin2
  N11: U3.Output, Piezo3.pin1, Piezo4.pin1
  N12: U3.Reset, C7.+, R8.Pin_1, J8.pin1
  N13: U3.Control_Voltage, C6.1
  N14: U3.Threshold, R7.Pin_0
  N15: U3.Discharge, R8.Pin_0
  N16: LED6.cathode, LED7.anode
  N17: LED6.anode, R9.Pin_0
  N18: LED7.cathode, LED8.anode
  N19: LED8.cathode, LED9.anode
  N20: LED9.cathode, LED10.anode
  N21: LED10.cathode, J9.pin2
  N22: R9.Pin_1, J9.pin1

notes:
  12V LED
  Module
  modules attached
  in parallel
