# Fritzing sketch PIR (saved by Fritzing 0.9.4)
breadboards: 1

parts:
  PIR1 = PIR sensor
  PIR2 = PIR sensor
  PIR3 = PIR sensor
  D1 = Diode [package=diode-1n4148]
  D2 = Diode [package=diode-1n4148]
  D3 = Diode [package=diode-1n4148]
  R1 = Resistor [tolerance=±5% resistance=1k package=THT]
  J1 = screw terminal, 3 pins

nets:
  5V: PIR1.VDD, PIR2.VDD, PIR3.VDD, J1.pin1
  N1: PIR1.SIG, D1.A
  GND: PIR1.GND, PIR2.GND, PIR3.GND, R1.Pin_0, J1.pin3
  N2: PIR2.SIG, D2.A
  N3: PIR3.SIG, D3.A
  N4: D1.C, D2.C, D3.C, R1.Pin_1, J1.pin2
