# Fritzing sketch animal_det (saved by Fritzing 0.9.6b)
breadboards: 1

parts:
  IC1 = 24LC1025 [package=THT]  # not connected
  ATTINY26L = IC, DIP package, 20 pins [chip_label=IC]
  U1 = 556 [package=dil14]
  IC3 = Voltage Regulator [package=to-220-alt]
  R2 = Resistor [tolerance=±5% resistance=220 package="2010 [SMD]"]
  U2 = TRANSISTOR_NPN_2 [package=to-92]
  LED1 = LEDs [package=led10mm]
  R3 = Resistor [tolerance=±5% power=0.25 resistance=220 package=THT]
  R4 = Resistor [tolerance=±5% power=0.25 resistance=220 package=THT]
  LED2 = LEDs [package=led10mm]
  R5 = Resistor [tolerance=±5% power=0.25 resistance=220 package=THT]
  LED3 = LEDs [package=led10mm]
  R6 = Resistor [tolerance=±5% power=0.25 resistance=220 package=THT]
  LED4 = LEDs [package=led10mm]
  R7 = Resistor [tolerance=±5% power=0.25 resistance=220 package=THT]
  LED5 = LEDs [package=led10mm]
  R8 = Resistor [tolerance=±5% power=0.25 resistance=220 package=THT]
  SPKR1 = Loudspeaker
  SP1 = SPEAKER [package=pcb_mount_speaker]
  R10 = Resistor [tolerance=±5% power=0.25 resistance=220 package=THT]
  C1 = Ceramic Capacitor [capacitance=100nF voltage=35V package="100 mil [THT, multilayer]"]
  C2 = Ceramic Capacitor [capacitance=100nF voltage=35V package="100 mil [THT, multilayer]"]
  R11 = Resistor [tolerance=±5% power=0.25 resistance=220 package=THT]
  C3 = Ceramic Capacitor [capacitance=100nF voltage=35V package="100 mil [THT, multilayer]"]
  R12 = Resistor [tolerance=±5% power=0.25 resistance=220 package=THT]
  R13 = Resistor [tolerance=±5% power=0.25 resistance=220 package=THT]
  C4 = Ceramic Capacitor [capacitance=100nF voltage=35V package="100 mil [THT, multilayer]"]
  PIR0 = screw terminal, 3 pins
  PIR1 = screw terminal, 3 pins

nets:
  5V: ATTINY26L.pin5, ATTINY26L.pin15, PIR0.pin1, PIR1.pin1
  GND: ATTINY26L.pin6, ATTINY26L.pin16, U1.GND, IC3.GND, U2.E, SPKR1.pin2, SP1.-, C1.0, C2.0, C3.0, C4.0, PIR0.pin3, PIR1.pin3
  N1: ATTINY26L.pin7, R2.Pin_1
  N2: ATTINY26L.pin9, PIR1.pin2
  N3: ATTINY26L.pin11, U1.RST
  N4: ATTINY26L.pin12, U1.RST2
  N5: ATTINY26L.pin17, PIR0.pin2
  N6: U1.DIS, R10.Pin_1, R11.Pin_0
  N7: U1.THR, U1.TRIG, C1.1, R11.Pin_1
  N8: U1.CV, C2.1
  N9: U1.OUT, SPKR1.pin1
  N10: U1.TRIG2, U1.THR2, C3.1, R13.Pin_1
  N11: U1.OUT2, SP1.+
  N12: U1.CV2, C4.1
  N13: U1.DIS2, R12.Pin_1, R13.Pin_0
  12V: U1.VCC, IC3.IN, R12.Pin_0
  N14: IC3.OUT, LED1.A, LED2.A, LED3.A, LED4.A, LED5.A
  N15: R2.Pin_0, U2.B
  N16: LED1.C, R4.Pin_0
  N17: R3.Pin_0, R4.Pin_1, R5.Pin_1, R6.Pin_1, R7.Pin_1, R8.Pin_1
  N18: LED2.C, R5.Pin_0
  N19: LED3.C, R6.Pin_0
  N20: LED4.C, R7.Pin_0
  N21: LED5.C, R8.Pin_0
