# Fritzing sketch ultrasonic (saved by Fritzing 0.9.4)
breadboards: 1

parts:
  Q1 = NPN-Transistor [package="TO92 [THT]"]
  R1 = Resistor [tolerance=±5% resistance=1k package=THT]
  U2 = 555 Timer [package="DIP8 [THT]"]
  C1 = Ceramic Capacitor [capacitance=1nF package="100 mil [THT, multilayer]"]
  C3 = Electrolytic Capacitor [capacitance=1µF package="100 mil [THT, electrolytic]"]
  R4 = Resistor [tolerance=±5% resistance=220 package=THT]
  R5 = Resistor [tolerance=±5% resistance=220 package=THT]
  Piezo1 = Piezo Speaker
  Piezo2 = Piezo Speaker
  C4 = Ceramic Capacitor [capacitance=0.1nF package="100 mil [THT, multilayer]"]  # not connected
  J1 = screw terminal, 3 pins

nets:
  GND: Q1.E, C1.0, C3.-, Piezo1.pin2, Piezo2.pin2, J1.pin3
  N1: Q1.B, R1.Pin_1
  N2: Q1.C, U2.Ground
  N3: R1.Pin_0, J1.pin2
  N4: U2.Output, Piezo1.pin1, Piezo2.pin1
  N5: U2.Reset, C3.+, R5.Pin_1, J1.pin1
  N6: U2.Control_Voltage, C1.1
  N7: U2.Threshold, R4.Pin_0
  N8: U2.Discharge, R5.Pin_0
  12V: U2.Vcc_Supply_Voltage
